# Fritzing sketch Diagrama_RCWL-0516 (saved by Fritzing 0.9.3b)

parts:
  Componente1 = Arduino Uno (Rev3)
  RCWL-0516_Microwave_Radar_Motion_Sensor1 = RCWL-0516 Microwave Radar Motion Sensor Module
  KY-1 = Keyes Relay [package=THT]

nets:
  N1: Componente1.D2, RCWL-0516_Microwave_Radar_Motion_Sensor1.OUT
  N2: Componente1.D3_PWM, KY-1.signal
  5V: Componente1.5V, RCWL-0516_Microwave_Radar_Motion_Sensor1.VIN, KY-1.power
  GND: Componente1.GND, RCWL-0516_Microwave_Radar_Motion_Sensor1.GND, KY-1.ground

custom parts:
  RCWL-0516 Microwave Radar Motion Sensor Module: The RCWL-0516 is a microwave radar motion sensor module. Input voltage is 4V to 28V. The 3V3 pin is a power output.
  Keyes Relay: The Keyes 5V relay module is suitable for SCM development, home appliance control. It uses a 5V~12V TIL control signal which can control DC / AC signal.
